# Fritzing sketch Actual Sketch 2 (saved by Fritzing 1.0.5)
breadboards: 1

parts:
  Part1 = Arduino Uno (Rev3)
  U1 = LCD-16X2 [package=lcd-16x2_noholes]
  M1 = Dagu DGServo 9g (Pan and tilt) [part_number=RS001B]
  S1 = Pushbutton [package="[THT]"]
  S2 = Pushbutton [package="[THT]"]
  R2 = Rotary Potentiometer (Small) [maximum_resistance=10kΩ knob_status=50% power=0.5W package=THT]
  Part2 = RFID-RC522-v2
  Keypad4x2 = Keypad Membran 4x4

nets:
  N1: Part1.A0, Keypad4x2.Pin1
  N2: Part1.A1, Keypad4x2.Pin2
  N3: Part1.A2, Keypad4x2.Pin5
  N4: Part1.A3, Keypad4x2.Pin6
  N5: Part1.A4/SDA, S1.Pin_1, S1.Pin_2
  N6: Part1.A5/SCL, S2.Pin_1, S2.Pin_2
  N7: Part1.D8, M1.pulse
  N8: Part1.D9_PWM, Part2.RST
  N9: Part1.D10_PWM/SS, Part2.SDA
  N10: Part1.D11_PWM/MOSI, Part2.MOSI
  N11: Part1.D12/MISO, Part2.MISO
  N12: Part1.D13/SCK, Part2.SCK
  N13: Part1.D2, U1.DB7
  N14: Part1.D3_PWM, U1.DB6
  N15: Part1.D4, U1.DB5
  N16: Part1.D5_PWM, U1.DB4
  N17: Part1.D6_PWM, U1.E
  N18: Part1.D7, U1.RS
  3V3: Part1.3V3, Part2.3.3V
  5V: Part1.5V, U1.VDD, U1.A, M1.vcc, R2.leg2
  GND: Part1.GND, U1.VSS, U1.R_W, U1.K, M1.gnd, S1.Pin_3, S1.Pin_4, S2.Pin_3, S2.Pin_4, R2.leg1, Part2.GND
  N19: U1.VO, R2.wiper

custom parts:
  RFID-RC522-v2: A simple China made RFID-RC522 Reader; do check the pin labels, as this is a MFRC522 based clone.
  Keypad Membran 4x4: Membrane Keypad 4x4 Matrix

// code stored in the sketch: smart_door_lock.ino
#include <SPI.h>
#include <MFRC522.h>
#include <Servo.h>
#include <LiquidCrystal.h>
#include <Keypad.h>

// ----------------------- PIN DEFINITIONS -----------------------
#define RST_PIN 9
#define SS_PIN 10
MFRC522 rfid(SS_PIN, RST_PIN);

Servo doorServo;

LiquidCrystal lcd(7, 6, 5, 4, 3, 2); // RS,E,D4,D5,D6,D7

// Keypad setup (2x2)
const byte ROWS = 2;
const byte COLS = 2;
char keys[ROWS][COLS] = {
  {'1','2'},
  {'3','4'}
};
byte rowPins[ROWS] = {A0, A1};
byte colPins[COLS] = {A2, A3};
Keypad keypad = Keypad(makeKeymap(keys), rowPins, colPins, ROWS, COLS);

// Buttons
#define MODE_BUTTON A4  // Enter password mode
#define INC_BUTTON  A5  // Update time/date from PC

#define SERVO_PIN 8

// ----------------------- GLOBAL VARIABLES -----------------------
String currentTime = "12:00";  // default
String currentDate = "01/01/26"; // default
String welcomeMsg = "Hello, welcome to the home of tech  ";
int scrollIndex = 0;

String authorizedPINs[] = {"12","34"}; // example 2x2 keypad PINs
String authorizedRFIDs[] = {"F1061B06","119D3206"}; // example RFID UIDs

bool inPasswordMode = false;
bool inUpdateMode = false;

// ----------------------- SETUP -----------------------
void setup() {
  Serial.begin(9600);
  SPI.begin();
  rfid.PCD_Init();
  doorServo.attach(SERVO_PIN);
  doorServo.write(0); // Locked

  pinMode(MODE_BUTTON, INPUT_PULLUP);
  pinMode(INC_BUTTON, INPUT_PULLUP);

  lcd.begin(16,2);
  lcd.clear();
}

// ----------------------- HELPER FUNCTIONS -----------------------

// Scroll welcome message
void scrollWelcome() {
  if(inPasswordMode || inUpdateMode) return; // pause scroll
  String displayStr = welcomeMsg.substring(scrollIndex);
  if(displayStr.length() < 16){
    displayStr += welcomeMsg.substring(0, 16 - displayStr.length());
  }
  lcd.setCursor(0,1);
  lcd.print(displayStr);
  scrollIndex++;
  if(scrollIndex >= welcomeMsg.length()) scrollIndex = 0;
}

// Display current time/date on line 1
void displayTimeDate() {
  if(!inPasswordMode && !inUpdateMode){
    lcd.setCursor(0,0);
    lcd.print(currentTime + " " + currentDate);
  }
}

// ----------------------- PASSWORD INPUT MODE -----------------------
bool enterPasswordMode() {
  lcd.clear();
  lcd.setCursor(0,0);
  lcd.print("Password input:");
  lcd.setCursor(0,1);
  String input = "";
  char key;
  unsigned long start = millis();

  while(millis() - start < 10000){ // 10s to enter PIN
    key = keypad.getKey();
    if(key){
      input += key;
      lcd.setCursor(input.length()-1,1);
      lcd.print("*"); // mask input
      if(input.length() >= 2){ // PIN length
        for(int i=0;i<sizeof(authorizedPINs)/sizeof(String);i++){
          if(input == authorizedPINs[i]){
            Serial.println("Access Granted via PIN: " + input);
            lcd.setCursor(0,1);
            lcd.print("ACCESS GRANTED  ");
            doorServo.write(90); // unlock
            delay(5000);
            doorServo.write(0); // lock
            return true;
          }
        }
        Serial.println("Access Denied via PIN: " + input);
        lcd.setCursor(0,1);
        lcd.print("ACCESS DENIED   ");
        delay(5000);
        return false;
      }
    }
  }
  return false;
}

// ----------------------- TIME/DATE UPDATE MODE -----------------------
void enterUpdateMode() {
  lcd.clear();
  lcd.setCursor(0,0);
  lcd.print("Update from PC");
  lcd.setCursor(0,1);
  lcd.print("Waiting...      ");

  // wait for Serial input in format HH:MM DD/MM/YY
  unsigned long start = millis();
  while(millis() - start < 15000){ // wait 15s max
    if(Serial.available()){
      String data = Serial.readStringUntil('\n');
      data.trim();
      if(data.length() >= 14){ // minimal validation
        currentTime = data.substring(0,5);
        currentDate = data.substring(6,14);
        Serial.println("Time/Date updated: " + currentTime + " " + currentDate);
        lcd.setCursor(0,1);
        lcd.print("Updated!       ");
        delay(2000);
        return;
      }
    }
  }
  lcd.setCursor(0,1);
  lcd.print("No input       ");
  delay(2000);
}

// ----------------------- RFID CHECK -----------------------
void checkRFID() {
  if(inPasswordMode || inUpdateMode) return;

  if (rfid.PICC_IsNewCardPresent() && rfid.PICC_ReadCardSerial()) {
    String rfidID = "";
    for(byte i=0; i<rfid.uid.size; i++){
      if(rfid.uid.uidByte[i] < 0x10) rfidID += "0";
      rfidID += String(rfid.uid.uidByte[i], HEX);
    }
    rfidID.toUpperCase();

    bool authorized = false;
    for(int i=0; i<sizeof(authorizedRFIDs)/sizeof(String); i++){
      if(rfidID == authorizedRFIDs[i]){
        authorized = true;
        break;
      }
    }

    lcd.clear();
    if(authorized){
      lcd.setCursor(0,0);
      lcd.print("ACCESS GRANTED");
      Serial.println("Access granted via RFID: " + rfidID);
      doorServo.write(90);
      delay(5000);
      doorServo.write(0);
    } else {
      lcd.setCursor(0,0);
      lcd.print("ACCESS DENIED");
      Serial.println("Access denied via RFID: " + rfidID);
      delay(5000);
    }

    lcd.clear();
    scrollIndex = 0;
    rfid.PICC_HaltA();
    rfid.PCD_StopCrypto1();
  }
}


// ----------------------- LOOP -----------------------
void loop() {
  displayTimeDate();
  scrollWelcome();

  // RFID check (automatic)
  checkRFID();

  // MODE button → password input
  if(digitalRead(MODE_BUTTON) == LOW){
    inPasswordMode = true;
    enterPasswordMode();
    inPasswordMode = false;
    lcd.clear();
    scrollIndex = 0;
    delay(200);
  }

  // INC button → update from PC
  if(digitalRead(INC_BUTTON) == LOW){
    inUpdateMode = true;
    enterUpdateMode();
    inUpdateMode = false;
    lcd.clear();
    scrollIndex = 0;
    delay(200);
  }

  delay(300); // scroll speed
}
